# Fritzing sketch YemekKartiProject (saved by Fritzing 0.9.6b)

parts:
  Parça1 = Arduino Uno (Rev3)
  LED1 = smd LED [color="Green (570nm)" package="0805 [SMD]"]  # not connected
  LED2 = smd LED [color="Red (635nm)" package="0805 [SMD]"]  # not connected
  microSD1 = MicroSD Card Module
  J1 = Piezo Speaker
  Parça2 = RFID-RC522-v2
  R3 = Resistor [tolerance=±5% power=0.25 resistance=330 package=THT]
  R4 = Resistor [tolerance=±5% power=0.25 resistance=330 package=THT]
  R5 = Resistor [tolerance=±5% power=0.25 resistance=330 package=THT]
  MH-Real-Time_Clock_Module_3 = RTC_DS1302_module

nets:
  N1: Parça1.D8, MH-Real-Time_Clock_Module_3.CLK
  N2: Parça1.D9_PWM, MH-Real-Time_Clock_Module_3.DAT
  N3: Parça1.D10_PWM/SS, Parça2.SDA
  N4: Parça1.D11_PWM/MOSI, microSD1.MOSI
  N5: Parça1.D12/MISO, R5.Pin_1
  N6: Parça1.D13/SCK, microSD1.SCK
  N7: Parça1.D3_PWM, MH-Real-Time_Clock_Module_3.RST
  N8: Parça1.D4, microSD1.CS
  N9: Parça1.D5_PWM, R4.Pin_0
  N10: Parça1.D6_PWM, R3.Pin_0
  N11: Parça1.D7, J1.pin2
  3V3: Parça1.3V3, Parça2.3.3V
  5V: Parça1.5V, microSD1.VCC
  GND: Parça1.GND, microSD1.GND
  N12: microSD1.MISO, R5.Pin_0

notes:
  mosi
  miso
  sck

custom parts:
  RFID-RC522-v2: A simple China made RFID-RC522 Reader; do check the pin labels, as this is a MFRC522 based clone.
  RTC_DS1302_module: Arduino module DS1302 SPI Real Time Clock
